# Fritzing sketch Breadboard (saved by Fritzing 0.9.3b)
breadboards: 1

parts:
  Part1 = Arduino Due (Rev2b)
  Mod1 = CJMCU-811
  OLED_I2C1 = OLED 128x64 I2C Monochrome Display

nets:
  VCC: Part1.IOREF, Mod1.VCC, OLED_I2C1.VDD
  GND: Part1.GND, Mod1.GND, OLED_I2C1.GND
  N1: Part1.SDA1, Part1.SCL1, Mod1.SDA, OLED_I2C1.SDA, OLED_I2C1.SCK

custom parts:
  CJMCU-811: The CCS811 is an ultra-low power digital gas sensor solution which integrates a metal oxide (MOX) gas sensor to detect a wide range of Volatile Organic Compounds (VOCs) for indoor air quality monitoring with a microcontroller unit (MCU), which includes an Analog-to-Digital converter (ADC), and an I²C interface.
